// Logisim project ALU.circ as structural Verilog: 1 circuit, main circuit ALU
module ALU (
  input  [3:0] A_3_0,
  input  [3:0] B_3_0,
  input  Cin,
  input  Logic_nArith,
  input  nInvert,
  input  nA_Only,
  output [3:0] Y_3_0,
  output Cout,
  output OF
);

  wire not_1_out;
  wire [3:0] not_neg_1_y_3_0;

  not not_1 (not_1_out, nInvert);
  NOT_NEG not_neg_1 (.A_3_0(A_3_0), .nPass(not_1_out), .NOT_nNEG(Logic_nArith), .Y_3_0(not_neg_1_y_3_0));  // open: CRY
  AND_ADD and_add_1 (
    .A_3_0(not_neg_1_y_3_0), .B_3_0(B_3_0), .AND_nAdd(Logic_nArith), .nPass(nA_Only), .Cin(Cin),
    .Y_3_0(Y_3_0), .Cout(Cout), .OF(OF));
endmodule
