// Logisim project ANDADD.circ as structural Verilog: 1 circuit, main circuit AND/ADD
module AND_ADD (
  input  [3:0] A_3_0,
  input  [3:0] B_3_0,
  input  AND_nAdd,
  input  nPass,
  input  Cin,
  output [3:0] Y_3_0,
  output Cout,
  output OF
);

  wire not_1_out, not_2_out;
  wire [3:0] and_4_out, fa_4_1_a0_2, multiplexer_1_out;

  and and_1 (and_4_out[3], A_3_0[3], B_3_0[3]);
  and and_2 (and_4_out[2], A_3_0[2], B_3_0[2]);
  and and_3 (and_4_out[1], A_3_0[1], B_3_0[1]);
  and and_4 (and_4_out[0], A_3_0[0], B_3_0[0]);
  FA_4 fa_4_1 (
    .Cin(Cin), .Cout(Cout), .B0(B_3_0[0]), .B1(B_3_0[1]), .B2(B_3_0[2]), .B3(B_3_0[3]), .A2(A_3_0[2]),
    .A1(A_3_0[1]), .A0(A_3_0[0]), .A3(A_3_0[3]), .A0_2(fa_4_1_a0_2[0]), .A1_2(fa_4_1_a0_2[1]),
    .A2_2(fa_4_1_a0_2[2]), .A3_2(fa_4_1_a0_2[3]), .OF(OF));
  Multiplexer #(.width(4), .enable("false")) multiplexer_1 (
    .in0(and_4_out), .in1(fa_4_1_a0_2), .out(multiplexer_1_out), .sel(not_1_out));
  not not_1 (not_1_out, AND_nAdd);
  Multiplexer #(.width(4), .enable("false")) multiplexer_2 (
    .in0(multiplexer_1_out), .in1(A_3_0), .out(Y_3_0), .sel(not_2_out));
  not not_2 (not_2_out, nPass);
endmodule
