// Logisim project CPU.circ as structural Verilog: 9 circuits, main circuit ROM_4
module ALC (
  input  [3:0] in_1
);

  wire [15:0] decoder_1_out0;

  Hex_Digit_Display hex_digit_display_1 (.value(in_1));  // open: dp
  Decoder #(.select(4), .enable("false")) decoder_1 (
    .out0(decoder_1_out0[0]), .out1(decoder_1_out0[1]), .out2(decoder_1_out0[2]), .out3(decoder_1_out0[3]),
    .out4(decoder_1_out0[4]), .out5(decoder_1_out0[5]), .out6(decoder_1_out0[6]), .out7(decoder_1_out0[7]),
    .out8(decoder_1_out0[8]), .out9(decoder_1_out0[9]), .out10(decoder_1_out0[10]),
    .out11(decoder_1_out0[11]), .out12(decoder_1_out0[12]), .out13(decoder_1_out0[13]),
    .out14(decoder_1_out0[14]), .out15(decoder_1_out0[15]), .sel(in_1));
endmodule

module ROM_4 (
  input  [3:0] in_1,
  input  READ
);

  wire and_1_out, not_1_out;
  wire [3:0] rom_1_data;

  not not_1 (not_1_out, in_1[3]);
  and and_1 (and_1_out, not_1_out, READ);
  ROM #(.addrWidth(3), .dataWidth(4)) rom_1 (.addr(in_1[2:0]), .data(rom_1_data), .sel(and_1_out));
  Hex_Digit_Display hex_digit_display_1 (.value(rom_1_data));  // open: dp

  // Notes on the sheet:
  //   contents of rom_1 (hex, n*v repeats v):
  //   0 2
endmodule

module OUT_4 (
  input  [3:0] Data_Bus,
  input  Memory_Select,
  input  Write,
  input  Clock,
  input  Reset
);

  wire and_1_out;
  wire [3:0] register_1_q;

  and and_1 (and_1_out, Memory_Select, Write);
  Hex_Digit_Display hex_digit_display_1 (.value(register_1_q));  // open: dp
  Register #(.width(4)) register_1 (.D(Data_Bus), .en(and_1_out), .Q(register_1_q), .clk(Clock), .clr(Reset));
endmodule

module RAM_4 (
  input  [3:0] Data_Bus,
  input  Memory_Select,
  input  Write,
  input  Read,
  input  Clock,
  input  Reset
);

  wire and_1_out, and_2_out;
  wire [3:0] controlled_buffer_1_out, register_1_q;

  and and_1 (and_1_out, Memory_Select, Write);
  and and_2 (and_2_out, Memory_Select, Read);
  Register #(.width(4)) register_1 (.D(Data_Bus), .en(and_1_out), .Q(register_1_q), .clk(Clock), .clr(Reset));
  assign controlled_buffer_1_out = and_2_out ? register_1_q : 4'bz;  // Controlled_Buffer controlled_buffer_1
endmodule

module BCPU (
  input  Logic_nArith,
  input  nInvert,
  input  nA_Only,
  input  Load_ACC,
  input  ACC_to_Data_Bus,
  input  Clock,
  input  Reset,
  output [3:0] out_8
);

  wire [3:0] alu_1_y_3_0, register_1_q;

  ALU alu_1 (
    .A_3_0(out_8), .B_3_0(register_1_q), .Cin(1'b0), .Logic_nArith(Logic_nArith), .nInvert(nInvert),
    .nA_Only(nA_Only), .Y_3_0(alu_1_y_3_0));  // open: Cout, OF
  Hex_Digit_Display hex_digit_display_1 (.value(alu_1_y_3_0));  // open: dp
  Register #(.width(4)) register_1 (.D(alu_1_y_3_0), .en(Load_ACC), .Q(register_1_q), .clk(Clock), .clr(Reset));
  Hex_Digit_Display hex_digit_display_2 (.value(register_1_q));  // open: dp
  assign out_8 = ACC_to_Data_Bus ? register_1_q : 4'bz;  // Controlled_Buffer controlled_buffer_1
  Hex_Digit_Display hex_digit_display_3 (.value(out_8));  // open: dp
endmodule

module BMP (
  input  [3:0] in_1,
  input  Logic_nArith,
  input  nInvert,
  input  nA_Only,
  input  Load_ACC,
  input  ACC_to_Data_Bus,
  input  Write,
  input  Read,
  input  Clock,
  input  Reset
);

  wire and_1_out, and_2_out, and_3_out, and_4_out, not_1_out;
  wire [3:0] alu_1_y_3_0, controlled_buffer_1_out, register_1_q, register_2_q, register_3_q;
  wire [15:0] decoder_1_out0;

  ALU alu_1 (
    .A_3_0(controlled_buffer_1_out), .B_3_0(register_1_q), .Cin(1'b0), .Logic_nArith(Logic_nArith),
    .nInvert(nInvert), .nA_Only(nA_Only), .Y_3_0(alu_1_y_3_0));  // open: Cout, OF
  Hex_Digit_Display hex_digit_display_1 (.value(alu_1_y_3_0));  // open: dp
  Register #(.width(4)) register_1 (.D(alu_1_y_3_0), .en(Load_ACC), .Q(register_1_q), .clk(Clock), .clr(Reset));
  Hex_Digit_Display hex_digit_display_2 (.value(register_1_q));  // open: dp
  assign controlled_buffer_1_out = ACC_to_Data_Bus ? register_1_q : 4'bz;  // Controlled_Buffer controlled_buffer_1
  Hex_Digit_Display hex_digit_display_3 (.value(in_1));  // open: dp
  Decoder #(.select(4), .enable("false")) decoder_1 (
    .out0(decoder_1_out0[0]), .out1(decoder_1_out0[1]), .out2(decoder_1_out0[2]), .out3(decoder_1_out0[3]),
    .out4(decoder_1_out0[4]), .out5(decoder_1_out0[5]), .out6(decoder_1_out0[6]), .out7(decoder_1_out0[7]),
    .out8(decoder_1_out0[8]), .out9(decoder_1_out0[9]), .out10(decoder_1_out0[10]),
    .out11(decoder_1_out0[11]), .out12(decoder_1_out0[12]), .out13(decoder_1_out0[13]),
    .out14(decoder_1_out0[14]), .out15(decoder_1_out0[15]), .sel(in_1));
  and and_1 (and_1_out, decoder_1_out0[14], Write);
  and and_2 (and_2_out, decoder_1_out0[15], Write);
  and and_3 (and_3_out, decoder_1_out0[15], Read);
  Register #(.width(4)) register_2 (
    .D(controlled_buffer_1_out), .en(and_1_out), .Q(register_2_q), .clk(Clock), .clr(Reset));
  Register #(.width(4)) register_3 (
    .D(controlled_buffer_1_out), .en(and_2_out), .Q(register_3_q), .clk(Clock), .clr(Reset));
  Hex_Digit_Display hex_digit_display_4 (.value(register_2_q));  // open: dp
  assign controlled_buffer_1_out = and_3_out ? register_3_q : 4'bz;  // Controlled_Buffer controlled_buffer_2
  Hex_Digit_Display hex_digit_display_5 (.value(controlled_buffer_1_out));  // open: dp
  not not_1 (not_1_out, in_1[3]);
  and and_4 (and_4_out, not_1_out, Read);
  ROM #(.addrWidth(3), .dataWidth(4)) rom_1 (.addr(in_1[2:0]), .data(controlled_buffer_1_out), .sel(and_4_out));

  // Notes on the sheet:
  //   contents of rom_1 (hex, n*v repeats v):
  //   3 5
endmodule

module MAG (
  input  [3:0] Data_Bus,
  input  Load_MAR,
  input  Use_PC,
  input  Clock,
  input  Reset,
  output [3:0] Address_Bus
);

  wire not_1_out;
  wire [3:0] inc_4_1_y0, register_1_q, register_2_q;

  inc_4 inc_4_1 (
    .A3(register_1_q[3]), .A2(register_1_q[2]), .A1(register_1_q[1]), .A0(register_1_q[0]), .INC(1'b1),
    .Y2(inc_4_1_y0[2]), .Y1(inc_4_1_y0[1]), .Y0(inc_4_1_y0[0]), .Y3(inc_4_1_y0[3]));  // open: CRY
  Register #(.width(4)) register_1 (.D(inc_4_1_y0), .en(Use_PC), .Q(register_1_q), .clk(Clock), .clr(Reset));
  Register #(.width(4)) register_2 (.D(Data_Bus), .en(Load_MAR), .Q(register_2_q), .clk(Clock), .clr(Reset));
  Hex_Digit_Display hex_digit_display_1 (.value(register_1_q));  // open: dp
  Hex_Digit_Display hex_digit_display_2 (.value(register_2_q));  // open: dp
  not not_1 (not_1_out, Use_PC);
  Multiplexer #(.width(4), .enable("false")) multiplexer_1 (
    .in0(register_1_q), .in1(register_2_q), .out(Address_Bus), .sel(not_1_out));
endmodule

module CON (
  input  [3:0] Data_Bus,
  input  Clock,
  input  Reset,
  output Unused,
  output Unused_2,
  output Unused_3,
  output Unused_4,
  output Logic_nArith,
  output nInvert,
  output nA_Only,
  output Use_PC,
  output Load_MAR,
  output Load_ACC,
  output ACC_to_Data_Bus,
  output Read,
  output Write,
  output Load_IR,
  output Next_State_Bit_1,
  output Next_State_Bit_0
);

  wire [1:0] register_2_q;
  wire [3:0] register_1_q;

  Register #(.width(4)) register_1 (.D(Data_Bus), .en(Load_IR), .Q(register_1_q), .clk(Clock), .clr(Reset));
  Register #(.width(2)) register_2 (
    .D({Next_State_Bit_1, Next_State_Bit_0}), .en(1'b1), .Q(register_2_q), .clk(Clock), .clr(Reset));
  Hex_Digit_Display hex_digit_display_1 (.value(register_1_q));  // open: dp
  Hex_Digit_Display hex_digit_display_2 (.value({2'b00, register_2_q}));  // open: dp
  ROM #(.addrWidth(6), .dataWidth(16)) rom_1 (
    .addr({register_1_q, register_2_q}),
    .data({Unused, Unused_2, Unused_3, Unused_4, Logic_nArith, nInvert, nA_Only, Use_PC, Load_MAR, Load_ACC, ACC_to_Data_Bus, Read, Write, Load_IR, Next_State_Bit_1, Next_State_Bit_0}));  // open: sel

  // Notes on the sheet:
  //   contents of rom_1 (hex, n*v repeats v):
  //   115 f50 0 0 115 750 0 0 115 1
endmodule

module MP (
  input  Reset
);

  wire and_1_out, and_2_out, and_3_out, and_4_out, Clock, not_1_out, not_2_out;
  wire [1:0] register_2_q;
  wire [2:0] multiplexer_1_out;
  wire [3:0] alu_1_y_3_0, controlled_buffer_1_out, inc_4_1_y0, register_1_q, register_3_q, register_4_q,
       register_5_q, register_6_q, register_7_q;
  wire [3:3] multiplexer_1_out_2;
  wire [15:0] decoder_1_out0, rom_1_data;

  inc_4 inc_4_1 (
    .A3(register_3_q[3]), .A2(register_3_q[2]), .A1(register_3_q[1]), .A0(register_3_q[0]), .INC(1'b1),
    .Y2(inc_4_1_y0[2]), .Y1(inc_4_1_y0[1]), .Y0(inc_4_1_y0[0]), .Y3(inc_4_1_y0[3]));  // open: CRY
  Hex_Digit_Display hex_digit_display_1 (.value(rom_1_data[15:12]));  // open: dp
  Hex_Digit_Display hex_digit_display_2 (.value(rom_1_data[11:8]));  // open: dp
  Register #(.width(4)) register_1 (
    .D(controlled_buffer_1_out), .en(rom_1_data[2]), .Q(register_1_q), .clk(Clock), .clr(Reset));
  Register #(.width(2)) register_2 (.D(rom_1_data[1:0]), .en(1'b1), .Q(register_2_q), .clk(Clock), .clr(Reset));
  Hex_Digit_Display hex_digit_display_3 (.value(rom_1_data[7:4]));  // open: dp
  Hex_Digit_Display hex_digit_display_4 (.value(rom_1_data[3:0]));  // open: dp
  Register #(.width(4)) register_3 (.D(inc_4_1_y0), .en(rom_1_data[8]), .Q(register_3_q), .clk(Clock), .clr(Reset));
  Register #(.width(4)) register_4 (
    .D(controlled_buffer_1_out), .en(rom_1_data[7]), .Q(register_4_q), .clk(Clock), .clr(Reset));
  ALU alu_1 (
    .A_3_0(controlled_buffer_1_out), .B_3_0(register_5_q), .Cin(1'b0), .Logic_nArith(rom_1_data[11]),
    .nInvert(rom_1_data[10]), .nA_Only(rom_1_data[9]), .Y_3_0(alu_1_y_3_0));  // open: Cout, OF
  Hex_Digit_Display hex_digit_display_5 (.value(register_1_q));  // open: dp
  Hex_Digit_Display hex_digit_display_6 (.value({2'b00, register_2_q}));  // open: dp
  Hex_Digit_Display hex_digit_display_7 (.value(register_3_q));  // open: dp
  Hex_Digit_Display hex_digit_display_8 (.value(register_4_q));  // open: dp
  not not_1 (not_1_out, rom_1_data[8]);
  Hex_Digit_Display hex_digit_display_9 (.value(alu_1_y_3_0));  // open: dp
  ROM #(.addrWidth(6), .dataWidth(16)) rom_1 (.addr({register_1_q, register_2_q}), .data(rom_1_data));  // open: sel
  Multiplexer #(.width(4), .enable("false")) multiplexer_1 (
    .in0(register_3_q), .in1(register_4_q), .out({multiplexer_1_out_2[3], multiplexer_1_out}), .sel(not_1_out));
  Register #(.width(4)) register_5 (.D(alu_1_y_3_0), .en(rom_1_data[6]), .Q(register_5_q), .clk(Clock), .clr(Reset));
  Hex_Digit_Display hex_digit_display_10 (.value(register_5_q));  // open: dp
  assign controlled_buffer_1_out = rom_1_data[5] ? register_5_q : 4'bz;  // Controlled_Buffer controlled_buffer_1
  Hex_Digit_Display hex_digit_display_11 (.value({multiplexer_1_out_2[3], multiplexer_1_out}));  // open: dp
  Decoder #(.select(4), .enable("false")) decoder_1 (
    .out0(decoder_1_out0[0]), .out1(decoder_1_out0[1]), .out2(decoder_1_out0[2]), .out3(decoder_1_out0[3]),
    .out4(decoder_1_out0[4]), .out5(decoder_1_out0[5]), .out6(decoder_1_out0[6]), .out7(decoder_1_out0[7]),
    .out8(decoder_1_out0[8]), .out9(decoder_1_out0[9]), .out10(decoder_1_out0[10]),
    .out11(decoder_1_out0[11]), .out12(decoder_1_out0[12]), .out13(decoder_1_out0[13]),
    .out14(decoder_1_out0[14]), .out15(decoder_1_out0[15]), .sel({multiplexer_1_out_2[3], multiplexer_1_out}));
  and and_1 (and_1_out, decoder_1_out0[14], rom_1_data[3]);
  and and_2 (and_2_out, decoder_1_out0[15], rom_1_data[3]);
  and and_3 (and_3_out, decoder_1_out0[15], rom_1_data[4]);
  Clock clock_1 (.out(Clock));
  Register #(.width(4)) register_6 (
    .D(controlled_buffer_1_out), .en(and_1_out), .Q(register_6_q), .clk(Clock), .clr(Reset));
  Register #(.width(4)) register_7 (
    .D(controlled_buffer_1_out), .en(and_2_out), .Q(register_7_q), .clk(Clock), .clr(Reset));
  Hex_Digit_Display hex_digit_display_12 (.value(register_6_q));  // open: dp
  assign controlled_buffer_1_out = and_3_out ? register_7_q : 4'bz;  // Controlled_Buffer controlled_buffer_2
  Hex_Digit_Display hex_digit_display_13 (.value(controlled_buffer_1_out));  // open: dp
  not not_2 (not_2_out, multiplexer_1_out_2[3]);
  and and_4 (and_4_out, not_2_out, rom_1_data[4]);
  ROM #(.addrWidth(3), .dataWidth(4)) rom_2 (.addr(multiplexer_1_out), .data(controlled_buffer_1_out), .sel(and_4_out));

  // Notes on the sheet:
  //   contents of rom_1 (hex, n*v repeats v):
  //   115 550 0 0 115 750 0 0 115 1 0 0 115 f50
  //   contents of rom_2 (hex, n*v repeats v):
  //   0 5 1 4 2
endmodule
