// Logisim project FA_4.circ as structural Verilog: 1 circuit, main circuit FA_4
module FA_4 (
  input  A3,
  input  A2,
  input  A1,
  input  A0,
  input  B3,
  input  B2,
  input  B1,
  input  B0,
  input  Cin,
  output A3_2,
  output A2_2,
  output A1_2,
  output A0_2,
  output Cout,
  output OF
);

  wire fa_1_2_cout, fa_1_3_cout, fa_1_4_cout;

  FA_1 fa_1_1 (.A(A3), .B(B3), .Cin(fa_1_2_cout), .SUM(A3_2), .Cout(Cout));
  FA_1 fa_1_2 (.A(A2), .B(B2), .Cin(fa_1_3_cout), .SUM(A2_2), .Cout(fa_1_2_cout));
  FA_1 fa_1_3 (.A(A1), .B(B1), .Cin(fa_1_4_cout), .SUM(A1_2), .Cout(fa_1_3_cout));
  FA_1 fa_1_4 (.A(A0), .B(B0), .Cin(Cin), .SUM(A0_2), .Cout(fa_1_4_cout));

  assign OF = Cout;
endmodule
