// Logisim project NOTNEG.circ as structural Verilog: 1 circuit, main circuit NOT/NEG
module NOT_NEG (
  input  [3:0] A_3_0,
  input  nPass,
  input  NOT_nNEG,
  output [3:0] Y_3_0,
  output CRY
);

  wire and_1_out, not_1_out, xor_1_out, xor_2_out, xor_3_out, xor_4_out;

  not not_1 (not_1_out, NOT_nNEG);
  xor xor_1 (xor_1_out, nPass, A_3_0[3]);
  xor xor_2 (xor_2_out, nPass, A_3_0[2]);
  xor xor_3 (xor_3_out, nPass, A_3_0[1]);
  xor xor_4 (xor_4_out, nPass, A_3_0[0]);
  and and_1 (and_1_out, nPass, not_1_out);
  inc_4 inc_4_1 (
    .A3(xor_1_out), .A2(xor_2_out), .A1(xor_3_out), .A0(xor_4_out), .INC(and_1_out), .Y2(Y_3_0[2]),
    .Y1(Y_3_0[1]), .Y0(Y_3_0[0]), .Y3(Y_3_0[3]), .CRY(CRY));
endmodule
