// Logisim project ha_1.circ as structural Verilog: 1 circuit, main circuit ha_1
module ha_1 (
  input  in_1,
  input  in_2,
  output SUM,
  output CRY
);

  wire and_1_out, and_2_out, not_1_out, not_2_out;

  not not_1 (not_1_out, in_1);
  not not_2 (not_2_out, in_2);
  and and_1 (and_1_out, not_1_out, in_2);
  and and_2 (and_2_out, in_1, not_2_out);
  and and_3 (CRY, in_2, in_1);
  or or_1 (SUM, and_1_out, and_2_out);
endmodule
