// Logisim project inc_4.circ as structural Verilog: 1 circuit, main circuit inc_4
module inc_4 (
  input  A3,
  input  A2,
  input  A1,
  input  A0,
  input  INC,
  output Y3,
  output CRY,
  output Y2,
  output Y1,
  output Y0
);

  wire ha_1_2_cry, ha_1_3_cry, ha_1_4_cry;

  ha_1 ha_1_1 (.in_1(A3), .in_2(ha_1_2_cry), .SUM(Y3), .CRY(CRY));
  ha_1 ha_1_2 (.in_1(A2), .in_2(ha_1_3_cry), .SUM(Y2), .CRY(ha_1_2_cry));
  ha_1 ha_1_3 (.in_1(A1), .in_2(ha_1_4_cry), .SUM(Y1), .CRY(ha_1_3_cry));
  ha_1 ha_1_4 (.in_1(A0), .in_2(INC), .SUM(Y0), .CRY(ha_1_4_cry));
endmodule
